# Fritzing sketch circuit-schematic (saved by Fritzing 0.9.3b)
breadboards: 1

parts:
  Part1 = Arduino Mega 2560 (Rev3)
  S1 = H-Bridge with L298N
  Raspberry_Pi_1 = Raspberry Pi 3 [part_number=RPI-3-V1.2]  # not connected
  VCC1 = Battery block 9V
  M2 = DC Motor

nets:
  5V: Part1.5V, S1.5V
  N1: Part1.GND, VCC1.-
  N2: Part1.D2_PWM, S1.IN1
  N3: Part1.D3_PWM, S1.IN2
  N4: S1.12V, VCC1.+
  N5: S1.M1-01, M2.pin_1
  N6: S1.M1-02, M2.pin_2

notes:
  First two wires, green & black for one winding
  Seond pair of wiring for second winding
  OUT1 and OUT2
  OUT3 & OUT4
  PIN 8-11
  PINS TO IN1,IN2,IN3,IN4

custom parts:
  H-Bridge with L298N: h-bridge

// code stored in the sketch: test_pump.ino
// Arduino Mega Serial-Controlled DC Motor
// Uses L298N motor driver
// Press 'f' in Serial Monitor to activate the motor
// Press 's' in Serial Monitor to stop the motor

// L298N Motor Driver Pins
//const int motorEnable = 9;  // Enable pin for motor speed control
const int motorPin1 = 2;    // Motor control pin 1
const int motorPin2 = 3;    // Motor control pin 2

// Variables for serial control
char receivedChar;
boolean motorRunning = false;

void setup() {
  // Set motor control pins as outputs
//  pinMode(motorEnable, OUTPUT);
  pinMode(motorPin1, OUTPUT);
  pinMode(motorPin2, OUTPUT);
  
  // Initialize serial communication
  Serial.begin(9600);
  Serial.println("Serial-controlled motor ready");
  Serial.println("Press 'f' to start motor, 's' to stop");
  
  // Ensure motor is off at startup
  stopMotor();
}

void loop() {
  // Check if serial data is available
  if (Serial.available() > 0) {
    // Read the incoming byte
    receivedChar = Serial.read();
    
    // Check if the received character is 'f' (start motor)
    if (receivedChar == 'f') {
      startMotor();
      Serial.println("Motor ON");
    } 
    // Check if the received character is 's' (stop motor)
    else if (receivedChar == 's') {
      stopMotor();
      Serial.println("Motor OFF");
    }

    // Clear any remaining characters in the buffer
    while (Serial.available() > 0) {
      Serial.read();
    }
  }
}

// Function to start the motor
void startMotor() {
  // Set motor direction (forward)
  digitalWrite(motorPin1, HIGH);
  digitalWrite(motorPin2, LOW);
  
  // Set motor speed (0-255)
//  analogWrite(motorEnable, 200);  // ~75% speed
  
  motorRunning = true;
}

// Function to stop the motor
void stopMotor() {
  digitalWrite(motorPin1, LOW);
  digitalWrite(motorPin2, LOW);
//  analogWrite(motorEnable, 0);
  
  motorRunning = false;
}
